// Logisim project projectMy13 (1).circ as structural Verilog: 7 circuits, main circuit main
module main (
);

  wire and_1_out, and_2_out, and_3_out, clk, clk_2, comparator_5_gt, comparator_6_gt, d_i, mem, not_1_out,
       pos, R_out, r_w, selRAM, vxy, vxyDir, x, xPos, y;
  wire [2:0] register_1_q;
  wire [3:0] A, B;
  wire [4:0] joystick_1_y, kinematic_1_cheap_id, kinematic_1_l_bat_2, kinematic_1_r_bat_2,
       kinematic_1_x_ball1, kinematic_1_y_ball1, mmf, mmf1, mmf2, not_2_out, subtractor_1_out,
       subtractor_2_out, video_subsystem_1_ballx_2, video_subsystem_1_bally_2, video_subsystem_1_cheapid_2,
       video_subsystem_1_leftbaty_2, video_subsystem_1_rightbaty_2, video_subsystem_2_ballx_2,
       video_subsystem_2_bally_2, video_subsystem_2_cheapid_2, video_subsystem_2_leftbaty_2,
       video_subsystem_2_rightbaty_2, video_subsystem_3_ballx_2, video_subsystem_3_bally_2,
       video_subsystem_3_cheapid_2, video_subsystem_3_leftbaty_2, video_subsystem_3_rightbaty_2;
  wire [6:0] kinematic_1_x_ball;
  wire [7:0] adr, cdm_8_mark5_1_p6, cdm_8_mark5_1_p7, controlled_buffer_1_out, kinematic_1_vxy,
       kinematic_1_y_ball;
  wire [31:0] video_subsystem_1_out_6, video_subsystem_1_out_7, video_subsystem_1_out_8,
       video_subsystem_1_out_9, video_subsystem_1_out_10, video_subsystem_1_out_11, video_subsystem_1_out_12,
       video_subsystem_1_out_13, video_subsystem_2_out_6, video_subsystem_2_out_7, video_subsystem_2_out_8,
       video_subsystem_2_out_9, video_subsystem_2_out_10, video_subsystem_2_out_11, video_subsystem_2_out_12,
       video_subsystem_2_out_13, video_subsystem_3_out_6, video_subsystem_3_out_7, video_subsystem_3_out_8,
       video_subsystem_3_out_9, video_subsystem_3_out_10, video_subsystem_3_out_11, video_subsystem_3_out_12,
       video_subsystem_3_out_13, video_subsystem_4_out_6, video_subsystem_4_out_7, video_subsystem_4_out_8,
       video_subsystem_4_out_9, video_subsystem_4_out_10, video_subsystem_4_out_11, video_subsystem_4_out_12,
       video_subsystem_4_out_13;

  // CdM_8_mark5 cdm_8_mark5_1: pin names not known; wires that end beside it: clk, d_i, mem, r_w, adr, cdm_8_mark5_1_p6, cdm_8_mark5_1_p7
  Comparator comparator_1 (.a(adr), .b(8'hf6), .eq(pos));  // open: gt, lt
  Comparator comparator_2 (.a(adr), .b(8'hf4), .eq(x));  // open: gt, lt
  Comparator comparator_3 (.a(adr), .b(8'hf5), .eq(y));  // open: gt, lt
  Comparator comparator_4 (.a(adr), .b(8'hf3), .eq(vxy));  // open: gt, lt
  and and_1 (and_1_out, mem, ~d_i);  // AND_Gate
  not not_1 (not_1_out, r_w);
  assign controlled_buffer_1_out = not_1_out ? cdm_8_mark5_1_p6 : 8'bz;  // Controlled_Buffer controlled_buffer_1
  assign cdm_8_mark5_1_p7 = r_w ? controlled_buffer_1_out : 8'bz;  // Controlled_Buffer controlled_buffer_2
  Subtractor #(.width(5)) subtractor_1 (.a(mmf), .b(5'b00001), .out(subtractor_1_out));  // open: bin, bout
  Comparator #(.width(5), .mode("unsigned")) comparator_5 (
    .a(mmf), .b({5{1'b0}}), .gt(comparator_5_gt));  // open: eq, lt
  and and_2 (and_2_out, selRAM, d_i, mem);
  Multiplexer #(.width(5), .disabled(0), .enable("false")) multiplexer_1 (
    .in0(mmf), .in1(subtractor_1_out), .out(mmf1), .sel(comparator_5_gt));
  ROM rom_1 (.addr(adr), .data(controlled_buffer_1_out), .sel(and_1_out));
  RAM ram_1 (.addr(adr), .data(controlled_buffer_1_out), .sel(and_2_out), .clk(clk), .ld(r_w));  // open: clr
  // Probe on {mmf, register_1_q}
  Subtractor #(.width(5)) subtractor_2 (.a(mmf1), .b(5'b00001), .out(subtractor_2_out));  // open: bin, bout
  Register register_1 (.D(controlled_buffer_1_out), .en(and_3_out), .Q({mmf, register_1_q}), .clk(clk));  // open: clr
  and and_3 (and_3_out, ~r_w, d_i, ~vxyDir, pos, ~xPos);  // AND_Gate
  // Probe on {mmf, register_1_q}
  Multiplexer #(.width(5), .disabled(0), .enable("false")) multiplexer_2 (
    .in0(mmf1), .in1(subtractor_2_out), .out(mmf2), .sel(comparator_6_gt));
  Comparator #(.width(5), .mode("unsigned")) comparator_6 (
    .a(mmf1), .b(5'b11101), .gt(comparator_6_gt));  // open: eq, lt
  assign controlled_buffer_1_out = vxy ? {kinematic_1_vxy[7:6], vxyDir, kinematic_1_vxy[4:0]} : 8'bz;  // Controlled_Buffer controlled_buffer_3
  // Probe on mmf2
  nor nor_1 (selRAM, vxy, y, x);
  assign controlled_buffer_1_out = x ? {xPos, kinematic_1_x_ball} : 8'bz;  // Controlled_Buffer controlled_buffer_4
  assign controlled_buffer_1_out = y ? kinematic_1_y_ball : 8'bz;  // Controlled_Buffer controlled_buffer_5
  // Probe on mmf2
  // Probe on {xPos, kinematic_1_x_ball}
  // Probe on {kinematic_1_vxy[7:6], vxyDir, kinematic_1_vxy[4:0]}
  // Probe on {kinematic_1_vxy[7:6], vxyDir, kinematic_1_vxy[4:0]}
  // Probe on {xPos, kinematic_1_x_ball}
  Hex_Digit_Display hex_digit_display_1 (.value(A));  // open: dp
  Joystick #(.bits(5)) joystick_1 (.y(joystick_1_y));  // open: x
  Button R (.out(R_out));
  assign not_2_out = ~joystick_1_y;  // NOT_Gate not_2, 5 bits wide
  kinematic kinematic_1 (
    .X_ball({xPos, kinematic_1_x_ball}), .Y_ball(kinematic_1_y_ball),
    .vxy({kinematic_1_vxy[7:6], vxyDir, kinematic_1_vxy[4:0]}), .R_bat(mmf2), .reset(R_out),
    .L_bat(not_2_out), .clock(clk_2), .A_score(A), .B_score(B), .cheap_ID(kinematic_1_cheap_id),
    .X_ball1(kinematic_1_x_ball1), .Y_ball1(kinematic_1_y_ball1), .l_bat_2(kinematic_1_l_bat_2),
    .r_bat_2(kinematic_1_r_bat_2));
  // Probe on kinematic_1_y_ball
  DotMatrix #(.matrixcols(32), .matrixrows(32)) dotmatrix_1 (
    .col0(video_subsystem_1_out_6), .col1(video_subsystem_1_out_7), .col2(video_subsystem_1_out_8),
    .col3(video_subsystem_1_out_9), .col4(video_subsystem_1_out_10), .col5(video_subsystem_1_out_11),
    .col6(video_subsystem_1_out_12), .col7(video_subsystem_1_out_13), .col8(video_subsystem_2_out_6),
    .col9(video_subsystem_2_out_7), .col10(video_subsystem_2_out_8), .col11(video_subsystem_2_out_9),
    .col12(video_subsystem_2_out_10), .col13(video_subsystem_2_out_11), .col14(video_subsystem_2_out_12),
    .col15(video_subsystem_2_out_13), .col16(video_subsystem_3_out_6), .col17(video_subsystem_3_out_7),
    .col18(video_subsystem_3_out_8), .col19(video_subsystem_3_out_9), .col20(video_subsystem_3_out_10),
    .col21(video_subsystem_3_out_11), .col22(video_subsystem_3_out_12), .col23(video_subsystem_3_out_13),
    .col24(video_subsystem_4_out_6), .col25(video_subsystem_4_out_7), .col26(video_subsystem_4_out_8),
    .col27(video_subsystem_4_out_9), .col28(video_subsystem_4_out_10), .col29(video_subsystem_4_out_11),
    .col30(video_subsystem_4_out_12), .col31(video_subsystem_4_out_13));
  Clock clock_1 (.out(clk));
  // Probe on kinematic_1_y_ball
  video_subsystem video_subsystem_1 (
    .cheapID(kinematic_1_cheap_id), .ballX(kinematic_1_x_ball1), .ballY(kinematic_1_y_ball1),
    .leftBatY(kinematic_1_l_bat_2), .rightBatY(kinematic_1_r_bat_2), .cheapID_2(video_subsystem_1_cheapid_2),
    .ballX_2(video_subsystem_1_ballx_2), .ballY_2(video_subsystem_1_bally_2),
    .leftBatY_2(video_subsystem_1_leftbaty_2), .rightBatY_2(video_subsystem_1_rightbaty_2),
    .out_6(video_subsystem_1_out_6), .out_7(video_subsystem_1_out_7), .out_8(video_subsystem_1_out_8),
    .out_9(video_subsystem_1_out_9), .out_10(video_subsystem_1_out_10), .out_11(video_subsystem_1_out_11),
    .out_12(video_subsystem_1_out_12), .out_13(video_subsystem_1_out_13));
  Clock #(.highDuration(4), .lowDuration(4)) clock_2 (.out(clk_2));
  video_subsystem video_subsystem_2 (
    .cheapID(video_subsystem_1_cheapid_2), .ballX(video_subsystem_1_ballx_2),
    .ballY(video_subsystem_1_bally_2), .leftBatY(video_subsystem_1_leftbaty_2),
    .rightBatY(video_subsystem_1_rightbaty_2), .cheapID_2(video_subsystem_2_cheapid_2),
    .ballX_2(video_subsystem_2_ballx_2), .ballY_2(video_subsystem_2_bally_2),
    .leftBatY_2(video_subsystem_2_leftbaty_2), .rightBatY_2(video_subsystem_2_rightbaty_2),
    .out_6(video_subsystem_2_out_6), .out_7(video_subsystem_2_out_7), .out_8(video_subsystem_2_out_8),
    .out_9(video_subsystem_2_out_9), .out_10(video_subsystem_2_out_10), .out_11(video_subsystem_2_out_11),
    .out_12(video_subsystem_2_out_12), .out_13(video_subsystem_2_out_13));
  video_subsystem video_subsystem_3 (
    .cheapID(video_subsystem_2_cheapid_2), .ballX(video_subsystem_2_ballx_2),
    .ballY(video_subsystem_2_bally_2), .leftBatY(video_subsystem_2_leftbaty_2),
    .rightBatY(video_subsystem_2_rightbaty_2), .cheapID_2(video_subsystem_3_cheapid_2),
    .ballX_2(video_subsystem_3_ballx_2), .ballY_2(video_subsystem_3_bally_2),
    .leftBatY_2(video_subsystem_3_leftbaty_2), .rightBatY_2(video_subsystem_3_rightbaty_2),
    .out_6(video_subsystem_3_out_6), .out_7(video_subsystem_3_out_7), .out_8(video_subsystem_3_out_8),
    .out_9(video_subsystem_3_out_9), .out_10(video_subsystem_3_out_10), .out_11(video_subsystem_3_out_11),
    .out_12(video_subsystem_3_out_12), .out_13(video_subsystem_3_out_13));
  video_subsystem video_subsystem_4 (
    .cheapID(video_subsystem_3_cheapid_2), .ballX(video_subsystem_3_ballx_2),
    .ballY(video_subsystem_3_bally_2), .leftBatY(video_subsystem_3_leftbaty_2),
    .rightBatY(video_subsystem_3_rightbaty_2), .out_6(video_subsystem_4_out_6),
    .out_7(video_subsystem_4_out_7), .out_8(video_subsystem_4_out_8), .out_9(video_subsystem_4_out_9),
    .out_10(video_subsystem_4_out_10), .out_11(video_subsystem_4_out_11), .out_12(video_subsystem_4_out_12),
    .out_13(video_subsystem_4_out_13));  // open: cheapID_2, ballX_2, ballY_2, leftBatY_2, rightBatY_2
  Hex_Digit_Display hex_digit_display_2 (.value(B));  // open: dp

  // Notes on the sheet:
  //   contents of rom_1 (hex, n*v repeats v):
  //   d0 e0 d1 f4 b5 31 5 91 d2 0 d0 f3 b0 d3 7 4c d3 7 73 e1 1e d3 f5 bf 3d e2 1c 8e ee 9c d3 1 73 e1 2c
  //   d3 f5 bf 1d e3 2a 8e ee 9c d3 4 73 e1 42 95 e3 35 8e 95 e3 39 8e d3 f5 bf 3d e2 40 8e ee 9c d3 5 73
  //   e1 59 4 95 e3 4c 8e 11 e3 50 8e d3 f5 bf 3d e2 57 8e ee 9c d3 6 73 e1 6b 95 e3 62 8e d3 f5 bf 3d e2
  //   69 8e ee 9c d3 3 73 e1 82 4 95 e3 75 8e 11 e3 79 8e d3 f5 bf 1d e3 80 8e ee 9c d3 2 73 e1 94 95 e3
  //   8b 8e d3 f5 bf 1d e3 92 8e ee 9c d3 0 73 e1 9c d1 f5 b5 9a e3 a0 85 d0 f6 a1 ee 79*0 11 3d b2
endmodule

module video_subsystem (
  input  [4:0] cheapID,
  input  [4:0] ballX,
  input  [4:0] ballY,
  input  [4:0] leftBatY,
  input  [4:0] rightBatY,
  output [31:0] out_6,
  output [31:0] out_7,
  output [31:0] out_8,
  output [31:0] out_9,
  output [31:0] out_10,
  output [31:0] out_11,
  output [31:0] out_12,
  output [31:0] out_13,
  output [4:0] cheapID_2,
  output [4:0] ballX_2,
  output [4:0] ballY_2,
  output [4:0] leftBatY_2,
  output [4:0] rightBatY_2
);

  wire [4:0] video_chip_1_ballx_2, video_chip_1_bally_2, video_chip_1_chipid_2, video_chip_1_leftbaty_2,
       video_chip_1_rightbaty_2, video_chip_2_ballx_2, video_chip_2_bally_2, video_chip_2_chipid_2,
       video_chip_2_leftbaty_2, video_chip_2_rightbaty_2, video_chip_3_ballx_2, video_chip_3_bally_2,
       video_chip_3_chipid_2, video_chip_3_leftbaty_2, video_chip_3_rightbaty_2, video_chip_4_ballx_2,
       video_chip_4_bally_2, video_chip_4_chipid_2, video_chip_4_leftbaty_2, video_chip_4_rightbaty_2,
       video_chip_5_ballx_2, video_chip_5_bally_2, video_chip_5_chipid_2, video_chip_5_leftbaty_2,
       video_chip_5_rightbaty_2, video_chip_6_ballx_2, video_chip_6_bally_2, video_chip_6_chipid_2,
       video_chip_6_leftbaty_2, video_chip_6_rightbaty_2, video_chip_7_ballx_2, video_chip_7_bally_2,
       video_chip_7_chipid_2, video_chip_7_leftbaty_2, video_chip_7_rightbaty_2;

  video_chip video_chip_1 (
    .chipID(cheapID), .ballX(ballX), .ballY(ballY), .leftbatY(leftBatY), .rightbatY(rightBatY),
    .chipID_2(video_chip_1_chipid_2), .ballX_2(video_chip_1_ballx_2), .ballY_2(video_chip_1_bally_2),
    .leftbatY_2(video_chip_1_leftbaty_2), .rightbatY_2(video_chip_1_rightbaty_2), .out(out_6));
  video_chip video_chip_2 (
    .chipID(video_chip_1_chipid_2), .ballX(video_chip_1_ballx_2), .ballY(video_chip_1_bally_2),
    .leftbatY(video_chip_1_leftbaty_2), .rightbatY(video_chip_1_rightbaty_2),
    .chipID_2(video_chip_2_chipid_2), .ballX_2(video_chip_2_ballx_2), .ballY_2(video_chip_2_bally_2),
    .leftbatY_2(video_chip_2_leftbaty_2), .rightbatY_2(video_chip_2_rightbaty_2), .out(out_7));
  video_chip video_chip_3 (
    .chipID(video_chip_2_chipid_2), .ballX(video_chip_2_ballx_2), .ballY(video_chip_2_bally_2),
    .leftbatY(video_chip_2_leftbaty_2), .rightbatY(video_chip_2_rightbaty_2),
    .chipID_2(video_chip_3_chipid_2), .ballX_2(video_chip_3_ballx_2), .ballY_2(video_chip_3_bally_2),
    .leftbatY_2(video_chip_3_leftbaty_2), .rightbatY_2(video_chip_3_rightbaty_2), .out(out_8));
  video_chip video_chip_4 (
    .chipID(video_chip_3_chipid_2), .ballX(video_chip_3_ballx_2), .ballY(video_chip_3_bally_2),
    .leftbatY(video_chip_3_leftbaty_2), .rightbatY(video_chip_3_rightbaty_2),
    .chipID_2(video_chip_4_chipid_2), .ballX_2(video_chip_4_ballx_2), .ballY_2(video_chip_4_bally_2),
    .leftbatY_2(video_chip_4_leftbaty_2), .rightbatY_2(video_chip_4_rightbaty_2), .out(out_9));
  video_chip video_chip_5 (
    .chipID(video_chip_6_chipid_2), .ballX(video_chip_6_ballx_2), .ballY(video_chip_6_bally_2),
    .leftbatY(video_chip_6_leftbaty_2), .rightbatY(video_chip_6_rightbaty_2),
    .chipID_2(video_chip_5_chipid_2), .ballX_2(video_chip_5_ballx_2), .ballY_2(video_chip_5_bally_2),
    .leftbatY_2(video_chip_5_leftbaty_2), .rightbatY_2(video_chip_5_rightbaty_2), .out(out_11));
  video_chip video_chip_6 (
    .chipID(video_chip_4_chipid_2), .ballX(video_chip_4_ballx_2), .ballY(video_chip_4_bally_2),
    .leftbatY(video_chip_4_leftbaty_2), .rightbatY(video_chip_4_rightbaty_2),
    .chipID_2(video_chip_6_chipid_2), .ballX_2(video_chip_6_ballx_2), .ballY_2(video_chip_6_bally_2),
    .leftbatY_2(video_chip_6_leftbaty_2), .rightbatY_2(video_chip_6_rightbaty_2), .out(out_10));
  video_chip video_chip_7 (
    .chipID(video_chip_5_chipid_2), .ballX(video_chip_5_ballx_2), .ballY(video_chip_5_bally_2),
    .leftbatY(video_chip_5_leftbaty_2), .rightbatY(video_chip_5_rightbaty_2),
    .chipID_2(video_chip_7_chipid_2), .ballX_2(video_chip_7_ballx_2), .ballY_2(video_chip_7_bally_2),
    .leftbatY_2(video_chip_7_leftbaty_2), .rightbatY_2(video_chip_7_rightbaty_2), .out(out_12));
  video_chip video_chip_8 (
    .chipID(video_chip_7_chipid_2), .ballX(video_chip_7_ballx_2), .ballY(video_chip_7_bally_2),
    .leftbatY(video_chip_7_leftbaty_2), .rightbatY(video_chip_7_rightbaty_2), .chipID_2(cheapID_2),
    .ballX_2(ballX_2), .ballY_2(ballY_2), .leftbatY_2(leftBatY_2), .rightbatY_2(rightBatY_2), .out(out_13));
endmodule

module video_chip (
  input  [4:0] chipID,
  input  [4:0] ballX,
  input  [4:0] ballY,
  input  [4:0] leftbatY,
  input  [4:0] rightbatY,
  output [4:0] chipID_2,
  output [4:0] ballX_2,
  output [4:0] ballY_2,
  output [4:0] leftbatY_2,
  output [4:0] rightbatY_2,
  output [31:0] out
);

  wire comparator_1_eq, comparator_2_eq, comparator_3_eq;
  wire [31:0] multiplexer_1_out, multiplexer_2_out, multiplexer_3_out, shifter_1_out, shifter_2_out,
       shifter_3_out;

  Comparator #(.width(5)) comparator_1 (.a(chipID), .b(ballX), .eq(comparator_1_eq));  // open: gt, lt
  Comparator #(.width(5)) comparator_2 (.a(chipID), .b(5'b00011), .eq(comparator_2_eq));  // open: gt, lt
  Comparator #(.width(5)) comparator_3 (.a(5'b11100), .b(chipID), .eq(comparator_3_eq));  // open: gt, lt
  Adder #(.width(5)) adder_1 (.a(5'b00001), .b(chipID), .out(chipID_2));  // open: cin, cout
  Shifter #(.width(32)) shifter_1 (.in(32'h7), .\dist (leftbatY), .out(shifter_1_out));
  Shifter #(.width(32)) shifter_2 (.in(32'h7), .\dist (rightbatY), .out(shifter_2_out));
  Multiplexer #(.width(32), .enable("false")) multiplexer_1 (
    .in0({32{1'b0}}), .in1(shifter_1_out), .out(multiplexer_1_out), .sel(comparator_2_eq));
  Shifter #(.width(32)) shifter_3 (.in(32'h1), .\dist (ballY), .out(shifter_3_out));
  Multiplexer #(.width(32), .enable("false")) multiplexer_2 (
    .in0(multiplexer_1_out), .in1(shifter_2_out), .out(multiplexer_2_out), .sel(comparator_3_eq));
  Multiplexer #(.width(32), .enable("false")) multiplexer_3 (
    .in0({32{1'b0}}), .in1(shifter_3_out), .out(multiplexer_3_out), .sel(comparator_1_eq));
  // Probe on multiplexer_3_out
  // Probe on multiplexer_2_out
  assign out = multiplexer_3_out | multiplexer_2_out;  // OR_Gate or_1, 32 bits wide

  assign ballX_2 = ballX;
  assign ballY_2 = ballY;
  assign leftbatY_2 = leftbatY;
  assign rightbatY_2 = rightbatY;
endmodule

module kinematic (
  input  reset,
  input  [4:0] L_bat,
  input  [4:0] R_bat,
  input  clock,
  output [4:0] cheap_ID,
  output [7:0] X_ball,
  output [4:0] X_ball1,
  output [4:0] Y_ball1,
  output [7:0] Y_ball,
  output [4:0] l_bat_2,
  output [4:0] r_bat_2,
  output [7:0] vxy,
  output [3:0] A_score,
  output [3:0] B_score
);

  wire adder_1_cout, adder_2_cout, adder_7_cout, adder_8_cout, and_1_out, ball_contact_with_bat_1_bal_refl,
       ball_contact_with_bat_2_bal_refl, comparator_1_eq, comparator_2_eq, comparator_3_eq, comparator_4_eq,
       hit_Left_Side, hit_Right_Side, justContactWithBat, leftBatContact, not_3_out, not_4_out, not_5_out,
       not_6_out, or_1_out, or_2_out, relfX, relfY, righttBatContact;
  wire [2:0] multiplexer_5_out, multiplexer_6_out, vx_for_ball_1_out, vy_for_ball_1_out;
  wire [3:0] adder_3_out, adder_4_out, register_1_q, register_2_q;
  wire [7:0] adder_1_out, adder_2_out, adder_5_out, adder_6_out, multiplexer_3_out, multiplexer_4_out;

  Adder adder_1 (.a({{6{vxy[2]}}, vxy[1:0]}), .b(Y_ball), .out(adder_1_out), .cout(adder_1_cout));  // open: cin
  not not_1 (relfY, comparator_1_eq);
  Adder adder_2 (.a({{6{vxy[5]}}, vxy[4:3]}), .b(X_ball), .out(adder_2_out), .cout(adder_2_cout));  // open: cin
  not not_2 (relfX, comparator_2_eq);
  Register #(.width(4)) register_1 (.D(A_score), .en(hit_Right_Side), .Q(register_1_q), .clk(clock), .clr(reset));
  Register #(.width(4)) register_2 (.D(B_score), .en(hit_Left_Side), .Q(register_2_q), .clk(clock), .clr(reset));
  Comparator #(.width(1)) comparator_1 (.a(adder_1_cout), .b(vxy[2]), .eq(comparator_1_eq));  // open: gt, lt
  Comparator #(.width(1)) comparator_2 (.a(adder_2_cout), .b(vxy[5]), .eq(comparator_2_eq));  // open: gt, lt
  not not_3 (not_3_out, justContactWithBat);
  Multiplexer #(.width(4), .disabled(0), .enable("false")) multiplexer_1 (
    .in0(register_1_q), .in1(adder_3_out), .out(A_score), .sel(hit_Right_Side));
  Adder #(.width(4)) adder_3 (.a(register_1_q), .b(4'b0001), .out(adder_3_out));  // open: cin, cout
  Multiplexer #(.width(4), .disabled(0), .enable("false")) multiplexer_2 (
    .in0(register_2_q), .in1(adder_4_out), .out(B_score), .sel(hit_Left_Side));
  Adder #(.width(4)) adder_4 (.a(register_2_q), .b(4'b0001), .out(adder_4_out));  // open: cin, cout
  Multiplexer #(.width(8), .disabled(0), .enable("false")) multiplexer_3 (
    .in0(adder_1_out), .in1(8'h80), .out(multiplexer_3_out), .sel(reset));
  Multiplexer #(.width(8), .disabled(0), .enable("false")) multiplexer_4 (
    .in0(adder_2_out), .in1(8'h80), .out(multiplexer_4_out), .sel(reset));
  and and_1 (and_1_out, comparator_2_eq, not_3_out);
  Register register_3 (.D(multiplexer_3_out), .en(comparator_1_eq), .Q(Y_ball), .clk(clock));  // open: clr
  Register register_4 (.D(multiplexer_4_out), .en(and_1_out), .Q(X_ball), .clk(clock));  // open: clr
  vy_for_ball vy_for_ball_1 (.in(vxy[2:0]), .out(vy_for_ball_1_out));
  vx_for_ball vx_for_ball_1 (.in(vxy[5:3]), .out(vx_for_ball_1_out));
  Multiplexer #(.width(3), .disabled(0), .enable("false")) multiplexer_5 (
    .in0(vy_for_ball_1_out), .in1(3'b001), .out(multiplexer_5_out), .sel(reset));
  or or_1 (or_1_out, relfY, reset);
  Multiplexer #(.width(3), .disabled(0), .enable("false")) multiplexer_6 (
    .in0(vx_for_ball_1_out), .in1(3'b101), .out(multiplexer_6_out), .sel(reset));
  or or_2 (or_2_out, relfX, justContactWithBat, reset);
  Register #(.width(3)) register_5 (.D(multiplexer_5_out), .en(or_1_out), .Q(vxy[2:0]), .clk(clock));  // open: clr
  Register #(.width(3)) register_6 (.D(multiplexer_6_out), .en(or_2_out), .Q(vxy[5:3]), .clk(clock));  // open: clr
  and and_2 (hit_Left_Side, relfX, vxy[5]);
  Adder adder_5 (.a(X_ball), .b(8'he4), .out(adder_5_out));  // open: cin, cout
  Adder adder_6 (.a(X_ball), .b(8'h1c), .out(adder_6_out));  // open: cin, cout
  or or_3 (justContactWithBat, righttBatContact, leftBatContact);
  Adder adder_7 (.a(adder_5_out), .b({{6{vxy[5]}}, vxy[4:3]}), .cout(adder_7_cout));  // open: out, cin
  Comparator #(.width(1)) comparator_3 (.a(adder_7_cout), .b(vxy[5]), .eq(comparator_3_eq));  // open: gt, lt
  not not_4 (not_4_out, comparator_3_eq);
  ball_contact_with_bat ball_contact_with_bat_1 (
    .bat(L_bat), .Ycoor(Y_ball), .bal_refl(ball_contact_with_bat_1_bal_refl));
  Adder adder_8 (.a(adder_6_out), .b({{6{vxy[5]}}, vxy[4:3]}), .cout(adder_8_cout));  // open: out, cin
  not not_5 (not_5_out, comparator_4_eq);
  Comparator #(.width(1)) comparator_4 (.a(adder_8_cout), .b(vxy[5]), .eq(comparator_4_eq));  // open: gt, lt
  ball_contact_with_bat ball_contact_with_bat_2 (
    .bat(R_bat), .Ycoor(Y_ball), .bal_refl(ball_contact_with_bat_2_bal_refl));
  and and_3 (leftBatContact, not_4_out, ball_contact_with_bat_1_bal_refl);
  and and_4 (righttBatContact, not_5_out, ball_contact_with_bat_2_bal_refl);
  and and_5 (hit_Right_Side, relfX, not_6_out);
  not not_6 (not_6_out, vxy[5]);

  assign cheap_ID = {5{1'b0}};
  assign l_bat_2 = L_bat;
  assign r_bat_2 = R_bat;
  assign vxy[7:6] = 2'b00;
  assign X_ball1 = X_ball[7:3];
  assign Y_ball1 = Y_ball[7:3];

  // Other names for the same wires on the sheet: Lbat[4:0] = L_bat; Rbat[4:0] = R_bat; scoreA[3:0] = A_score;
  //   scoreB[3:0] = B_score; _3bitVX[2:0] = vxy[5:3]; vx[7:0] = {{6{vxy[5]}}, vxy[4:3]}; complVX = vxy[5];
  //   _3bitVY[2:0] = vxy[2:0]; vy[7:0] = {{6{vxy[2]}}, vxy[1:0]}; complVY = vxy[2]; Xcoor[7:0] = X_ball;
  //   Ycoor[7:0] = Y_ball
endmodule

module ball_contact_with_bat (
  input  [4:0] bat,
  input  [7:0] Ycoor,
  output bal_refl
);

  wire comparator_1_eq, comparator_2_eq, comparator_3_eq;
  wire [4:0] adder_1_out, adder_2_out;

  Adder #(.width(5)) adder_1 (.a(bat), .b(5'b00001), .out(adder_1_out));  // open: cin, cout
  Adder #(.width(5)) adder_2 (.a(bat), .b(5'b00010), .out(adder_2_out));  // open: cin, cout
  Comparator #(.width(5)) comparator_1 (.a(bat), .b(Ycoor[7:3]), .eq(comparator_1_eq));  // open: gt, lt
  Comparator #(.width(5)) comparator_2 (.a(adder_1_out), .b(Ycoor[7:3]), .eq(comparator_2_eq));  // open: gt, lt
  Comparator #(.width(5)) comparator_3 (.a(adder_2_out), .b(Ycoor[7:3]), .eq(comparator_3_eq));  // open: gt, lt
  or or_1 (bal_refl, comparator_1_eq, comparator_2_eq, comparator_3_eq);
endmodule

module vx_for_ball (
  input  [2:0] in,
  output [2:0] out
);

  wire comparator_1_eq;

  Comparator #(.width(3)) comparator_1 (.a(3'b010), .b(in), .eq(comparator_1_eq));  // open: gt, lt
  Multiplexer #(.width(3), .disabled(0), .enable("false")) multiplexer_1 (
    .in0(3'b010), .in1(3'b110), .out(out), .sel(comparator_1_eq));
endmodule

module vy_for_ball (
  input  [2:0] in,
  output [2:0] out
);

  wire comparator_1_eq;

  Comparator #(.width(3)) comparator_1 (.a(3'b001), .b(in), .eq(comparator_1_eq));  // open: gt, lt
  Multiplexer #(.width(3), .disabled(0), .enable("false")) multiplexer_1 (
    .in0(3'b001), .in1(3'b111), .out(out), .sel(comparator_1_eq));
endmodule
