// Logisim project NSU-FIT-2020-T04L1e04.circ as structural Verilog: 1 circuit, main circuit mycircuit
module mycircuit (
  input  A,
  input  B,
  input  C,
  output R
);

  wire not_1_out, or_1_out;

  not not_1 (not_1_out, A);
  or or_1 (or_1_out, B, C);
  and and_1 (R, not_1_out, not_1_out, or_1_out);
endmodule
