// Logisim project NSU-FIT-2020-T04L1e09.circ as structural Verilog: 1 circuit, main circuit mycircuit
module mycircuit (
  input  A,
  input  B,
  input  C,
  output R
);

  wire buffer_1_out, not_1_out;

  buf buffer_1 (buffer_1_out, A);
  not not_1 (not_1_out, C);
  and and_1 (R, buffer_1_out, not_1_out, not_1_out);
endmodule
