// Logisim project NSU-FIT-2020-T04L1e13.circ as structural Verilog: 1 circuit, main circuit mycircuit
module mycircuit (
  input  A,
  input  B,
  input  C,
  output R
);

  wire and_1_out, buffer_1_out;

  buf buffer_1 (buffer_1_out, A);
  and and_1 (and_1_out, B, C);
  or or_1 (R, buffer_1_out, and_1_out);
endmodule
