// Logisim project NSU-FIT-2020-T04L1e16.circ as structural Verilog: 1 circuit, main circuit mycircuit
module mycircuit (
  input  A,
  input  B,
  input  C,
  output R
);

  wire and_1_out, not_1_out, not_2_out;

  not not_1 (not_1_out, A);
  and and_1 (and_1_out, not_1_out, C);
  not not_2 (not_2_out, C);
  or or_1 (R, and_1_out, not_2_out);
endmodule
