// Logisim project NSU-FIT-2020-T04L2e02 (1).circ as structural Verilog: 1 circuit, main circuit formula
module formula (
  input  A,
  input  B,
  input  C,
  output R
);

  wire transistor_1_out;

  Transistor transistor_1 (.in(1'b1), .out(transistor_1_out), .gate(C));
  Transistor transistor_2 (.in(1'b1), .out(R), .gate(A));
  Pull_Resistor pull_resistor_1 (.node(R));
  Transistor transistor_3 (.in(transistor_1_out), .out(R), .gate(B));
endmodule
