// Logisim project NSU-FIT-2020-T05L2e03.circ as structural Verilog: 2 circuits, main circuit formula
module formula (
  input  [7:0] A,
  output [7:0] R,
  output OFL
);

  wire addder_1_bus_0_2, addder_2_bus_0_2, addder_3_bus_0_2, addder_4_bus_0_2;
  wire [7:0] addder_1_out, addder_2_out, addder_3_out;

  // Probe on A
  addder addder_1 (.cin(1'b0), .bus_0(A), .bus_1(A), .out(addder_1_out), .bus_0_2(addder_1_bus_0_2));
  addder addder_2 (
    .cin(addder_1_bus_0_2), .bus_0(addder_1_out), .bus_1(A), .out(addder_2_out), .bus_0_2(addder_2_bus_0_2));
  addder addder_3 (
    .cin(addder_2_bus_0_2), .bus_0(addder_2_out), .bus_1(A), .out(addder_3_out), .bus_0_2(addder_3_bus_0_2));
  addder addder_4 (.cin(addder_3_bus_0_2), .bus_0(addder_3_out), .bus_1(A), .out(R), .bus_0_2(addder_4_bus_0_2));
  // Probe on R
  or or_1 (OFL, addder_1_bus_0_2, addder_2_bus_0_2, addder_3_bus_0_2, addder_4_bus_0_2);
endmodule

module addder (
  input  cin,
  input  [7:0] bus_0,
  input  [7:0] bus_1,
  output [7:0] out,
  output bus_0_2
);

  wire and_1_out, and_2_out, and_3_out, and_4_out, and_5_out, and_6_out, and_7_out, and_8_out, and_9_out,
       and_10_out, and_11_out, and_12_out, and_13_out, and_14_out, and_15_out, and_16_out, or_1_out,
       or_2_out, or_3_out, or_4_out, or_5_out, or_6_out, or_7_out, xor_1_out, xor_3_out, xor_4_out,
       xor_6_out, xor_7_out, xor_11_out, xor_12_out, xor_13_out;

  xor xor_1 (xor_1_out, bus_0[0], bus_1[0]);
  xor xor_2 (out[0], xor_1_out, cin);
  and and_1 (and_1_out, cin, xor_1_out);
  and and_2 (and_2_out, bus_0[0], bus_1[0]);
  xor xor_3 (xor_3_out, bus_0[1], bus_1[1]);
  xor xor_4 (xor_4_out, bus_0[3], bus_1[3]);
  or or_1 (or_1_out, and_1_out, and_2_out);
  xor xor_5 (out[1], xor_3_out, or_1_out);
  and and_3 (and_3_out, or_1_out, xor_3_out);
  and and_4 (and_4_out, bus_0[1], bus_1[1]);
  xor xor_6 (xor_6_out, bus_0[2], bus_1[2]);
  xor xor_7 (xor_7_out, bus_0[4], bus_1[4]);
  or or_2 (or_2_out, and_3_out, and_4_out);
  xor xor_8 (out[2], xor_6_out, or_2_out);
  and and_5 (and_5_out, or_2_out, xor_6_out);
  and and_6 (and_6_out, bus_0[2], bus_1[2]);
  xor xor_9 (out[3], xor_4_out, or_4_out);
  and and_7 (and_7_out, or_4_out, xor_4_out);
  or or_3 (or_3_out, and_7_out, and_8_out);
  and and_8 (and_8_out, bus_0[3], bus_1[3]);
  xor xor_10 (out[4], xor_7_out, or_3_out);
  and and_9 (and_9_out, or_3_out, xor_7_out);
  and and_10 (and_10_out, bus_0[4], bus_1[4]);
  or or_4 (or_4_out, and_5_out, and_6_out);
  or or_5 (or_5_out, and_9_out, and_10_out);
  xor xor_11 (xor_11_out, bus_0[5], bus_1[5]);
  xor xor_12 (xor_12_out, bus_0[6], bus_1[6]);
  xor xor_13 (xor_13_out, bus_0[7], bus_1[7]);
  xor xor_14 (out[5], xor_11_out, or_5_out);
  and and_11 (and_11_out, or_5_out, xor_11_out);
  or or_6 (or_6_out, and_11_out, and_12_out);
  and and_12 (and_12_out, bus_0[5], bus_1[5]);
  xor xor_15 (out[6], xor_12_out, or_6_out);
  and and_13 (and_13_out, or_6_out, xor_12_out);
  and and_14 (and_14_out, bus_0[6], bus_1[6]);
  xor xor_16 (out[7], xor_13_out, or_7_out);
  and and_15 (and_15_out, or_7_out, xor_13_out);
  and and_16 (and_16_out, bus_0[7], bus_1[7]);
  or or_7 (or_7_out, and_13_out, and_14_out);
  or or_8 (bus_0_2, and_15_out, and_16_out);
endmodule
