// Logisim project NSU-FIT-2020-T05L2e05 (1).circ as structural Verilog: 2 circuits, main circuit bcd2
module bcd2 (
  input  Cin,
  input  [7:0] A,
  input  [7:0] B,
  output [7:0] R,
  output Cout
);

  wire bcd_add_1_cout;

  Hex_Digit_Display hex_digit_display_1 (.value(A[7:4]));  // open: dp
  Hex_Digit_Display hex_digit_display_2 (.value(B[7:4]));  // open: dp
  Hex_Digit_Display hex_digit_display_3 (.value({3'b000, Cin}));  // open: dp
  Hex_Digit_Display hex_digit_display_4 (.value(A[3:0]));  // open: dp
  Hex_Digit_Display hex_digit_display_5 (.value(B[3:0]));  // open: dp
  bcd_add bcd_add_1 (.Cin(Cin), .A(A[3:0]), .B(B[3:0]), .A_2(R[3:0]), .Cout(bcd_add_1_cout));
  bcd_add bcd_add_2 (.Cin(bcd_add_1_cout), .A(A[7:4]), .B(B[7:4]), .A_2(R[7:4]), .Cout(Cout));
  Hex_Digit_Display hex_digit_display_6 (.value({3'b000, Cout}));  // open: dp
  Hex_Digit_Display hex_digit_display_7 (.value(R[7:4]));  // open: dp
  Hex_Digit_Display hex_digit_display_8 (.value(R[3:0]));  // open: dp
endmodule

// BCD
module bcd_add (
  input  Cin,
  input  [3:0] A,
  input  [3:0] B,
  output [3:0] A_2,
  output Cout
);

  wire adder_1_cout, and_1_out, or_1_out;
  wire [3:0] adder_1_out;

  Adder #(.width(4)) adder_1 (.a(A), .b(B), .out(adder_1_out), .cin(Cin), .cout(adder_1_cout));
  or or_1 (or_1_out, adder_1_out[1], adder_1_out[2]);
  and and_1 (and_1_out, or_1_out, adder_1_out[3]);
  or or_2 (Cout, and_1_out, adder_1_cout);
  Adder #(.width(4)) adder_2 (.a(adder_1_out), .b({1'b0, {2{Cout}}, 1'b0}), .out(A_2));  // open: cin, cout
endmodule
