// Logisim project NSU-FIT-2020-T05L3e01 (2).circ as structural Verilog: 1 circuit, main circuit ALU
module ALU (
  input  Cin,
  input  [7:0] A,
  input  [7:0] B,
  input  [1:0] instr,
  output [7:0] R,
  output Cout,
  output V
);

  wire adder_1_cout, adder_2_cout, and_2_out, and_3_out, xnor_1_out, xor_1_out, xor_2_out, xor_3_out;
  wire [7:0] adder_1_out, adder_2_out, adder_3_out, adder_4_out, and_1_out, multiplexer_1_out, not_1_out,
       or_1_out;

  assign not_1_out = ~B;  // NOT_Gate not_1, 8 bits wide
  assign and_1_out = A & B;  // AND_Gate and_1, 8 bits wide
  assign or_1_out = A | B;  // OR_Gate or_1, 8 bits wide
  Adder adder_1 (.a(A), .b(not_1_out), .out(adder_1_out), .cin(Cin), .cout(adder_1_cout));
  xor xor_1 (xor_1_out, adder_2_out[7], A[7]);
  xnor xnor_1 (xnor_1_out, A[7], B[7]);
  xor xor_2 (xor_2_out, multiplexer_1_out[7], A[7]);
  xor xor_3 (xor_3_out, A[7], B[7]);
  Adder adder_2 (.a(A), .b(B), .out(adder_2_out), .cin(Cin), .cout(adder_2_cout));
  and and_2 (and_2_out, xor_1_out, xnor_1_out);
  and and_3 (and_3_out, xor_2_out, xor_3_out);
  Adder adder_3 (.a(8'h1), .b(adder_4_out), .out(adder_3_out));  // open: cin, cout
  Adder adder_4 (.a({{7{1'b0}}, Cin}), .b(adder_1_out), .out(adder_4_out));  // open: cin, cout
  Multiplexer #(.width(8), .enable("false")) multiplexer_1 (
    .in0(adder_3_out), .in1(adder_4_out), .out(multiplexer_1_out), .sel(Cin));
  Multiplexer #(.select(2), .width(8), .enable("false")) multiplexer_2 (
    .in0(and_1_out), .in1(or_1_out), .in2(adder_2_out), .in3(multiplexer_1_out), .out(R), .sel(instr));
  Multiplexer #(.select(2), .enable("false")) multiplexer_3 (
    .in0(1'b0), .in1(1'b0), .in2(adder_2_cout), .in3(adder_1_cout), .out(Cout), .sel(instr));
  Multiplexer #(.select(2), .enable("false")) multiplexer_4 (
    .in0(1'b0), .in1(1'b0), .in2(and_2_out), .in3(and_3_out), .out(V), .sel(instr));

  // Notes on the sheet:
  //   00: and
  //   01: or
  //   10: add
  //   11: sub
endmodule
