// Logisim project NSU-FIT-2020-T05L3e02.circ as structural Verilog: 4 circuits, main circuit cmp
module cmp (
  input  [7:0] A,
  input  [7:0] B,
  output Gt,
  output Eq
);

  more more_1 (.A(A), .B(B), .out_3(Gt));
  equal equal_1 (.A(A), .B(B), .out_3(Eq));

  // Notes on the sheet:
  //   A: pull=up
endmodule

module equal (
  input  [7:0] A,
  input  [7:0] B,
  output out_3
);

  wire xnor_1_out, xnor_2_out, xnor_3_out, xnor_4_out, xnor_5_out, xnor_6_out, xnor_7_out, xnor_8_out;

  xnor xnor_1 (xnor_1_out, A[0], B[0]);
  xnor xnor_2 (xnor_2_out, A[1], B[1]);
  xnor xnor_3 (xnor_3_out, A[2], B[2]);
  xnor xnor_4 (xnor_4_out, A[3], B[3]);
  xnor xnor_5 (xnor_5_out, A[4], B[4]);
  xnor xnor_6 (xnor_6_out, A[5], B[5]);
  xnor xnor_7 (xnor_7_out, A[6], B[6]);
  xnor xnor_8 (xnor_8_out, A[7], B[7]);
  and and_1 (out_3, xnor_1_out, xnor_2_out, xnor_3_out, xnor_4_out, xnor_5_out, xnor_6_out, xnor_7_out, xnor_8_out);
endmodule

module more (
  input  [7:0] A,
  input  [7:0] B,
  output out_3
);

  wire and_1_out, and_2_out, and_3_out, and_4_out, and_5_out, and_6_out, and_7_out, temp_1_eq, temp_1_mo,
       temp_2_eq, temp_2_mo, temp_3_eq, temp_3_mo, temp_4_eq, temp_4_mo, temp_5_eq, temp_5_mo, temp_6_eq,
       temp_6_mo, temp_7_eq, temp_7_mo, temp_8_eq, temp_8_mo;

  temp temp_1 (.A(A[7]), .B(B[7]), .mo(temp_1_mo), .eq(temp_1_eq));  // open: less
  temp temp_2 (.A(A[6]), .B(B[6]), .mo(temp_2_mo), .eq(temp_2_eq));  // open: less
  temp temp_3 (.A(A[5]), .B(B[5]), .mo(temp_3_mo), .eq(temp_3_eq));  // open: less
  temp temp_4 (.A(A[4]), .B(B[4]), .mo(temp_4_mo), .eq(temp_4_eq));  // open: less
  temp temp_5 (.A(A[3]), .B(B[3]), .mo(temp_5_mo), .eq(temp_5_eq));  // open: less
  temp temp_6 (.A(A[2]), .B(B[2]), .mo(temp_6_mo), .eq(temp_6_eq));  // open: less
  temp temp_7 (.A(A[1]), .B(B[1]), .mo(temp_7_mo), .eq(temp_7_eq));  // open: less
  temp temp_8 (.A(A[0]), .B(B[0]), .mo(temp_8_mo), .eq(temp_8_eq));  // open: less
  and and_1 (and_1_out, temp_1_eq, temp_2_eq, temp_3_eq, temp_4_eq, temp_5_eq, temp_6_eq, temp_7_mo);
  and and_2 (and_2_out, temp_1_eq, temp_2_eq, temp_3_eq, temp_4_eq, temp_5_eq, temp_6_eq, temp_7_eq, temp_8_mo);
  and and_3 (and_3_out, temp_1_eq, temp_2_eq, temp_3_eq, temp_4_mo);
  and and_4 (and_4_out, temp_1_eq, temp_2_eq, temp_3_eq, temp_4_eq, temp_5_mo);
  and and_5 (and_5_out, temp_1_eq, temp_2_eq, temp_4_eq, temp_3_eq, temp_5_eq, temp_6_mo);
  and and_6 (and_6_out, temp_1_eq, temp_2_mo);
  and and_7 (and_7_out, temp_1_eq, temp_2_eq, temp_3_mo);
  or or_1 (out_3, temp_1_mo, and_6_out, and_7_out, and_3_out, and_4_out, and_5_out, and_1_out, and_2_out);
endmodule

module temp (
  input  A,
  input  B,
  output mo,
  output eq,
  output less
);

  wire and_1_out, not_1_out, not_2_out;

  not not_1 (not_1_out, B);
  not not_2 (not_2_out, A);
  and and_1 (and_1_out, not_2_out, B);
  and and_2 (mo, A, not_1_out);
  xnor xnor_1 (eq, A, B);
  not not_3 (less, and_1_out);
endmodule
