// Logisim project project.circ as structural Verilog: 5 circuits, main circuit main
module main (
);

  wire clock_1_out, R_out;
  wire [3:0] A, B;
  wire [4:0] joystick_1_y, joystick_2_y, kinematic_1_cheap_id, kinematic_1_l_bat_2, kinematic_1_r_bat_2,
       kinematic_1_x_ball1, kinematic_1_y_ball1, not_1_out, not_2_out, video_subsystem_1_ballx_2,
       video_subsystem_1_bally_2, video_subsystem_1_cheapid_2, video_subsystem_1_leftbaty_2,
       video_subsystem_1_rightbaty_2, video_subsystem_2_ballx_2, video_subsystem_2_bally_2,
       video_subsystem_2_cheapid_2, video_subsystem_2_leftbaty_2, video_subsystem_2_rightbaty_2,
       video_subsystem_3_ballx_2, video_subsystem_3_bally_2, video_subsystem_3_cheapid_2,
       video_subsystem_3_leftbaty_2, video_subsystem_3_rightbaty_2;
  wire [31:0] video_subsystem_1_out_6, video_subsystem_1_out_7, video_subsystem_1_out_8,
       video_subsystem_1_out_9, video_subsystem_1_out_10, video_subsystem_1_out_11, video_subsystem_1_out_12,
       video_subsystem_1_out_13, video_subsystem_2_out_6, video_subsystem_2_out_7, video_subsystem_2_out_8,
       video_subsystem_2_out_9, video_subsystem_2_out_10, video_subsystem_2_out_11, video_subsystem_2_out_12,
       video_subsystem_2_out_13, video_subsystem_3_out_6, video_subsystem_3_out_7, video_subsystem_3_out_8,
       video_subsystem_3_out_9, video_subsystem_3_out_10, video_subsystem_3_out_11, video_subsystem_3_out_12,
       video_subsystem_3_out_13, video_subsystem_4_out_6, video_subsystem_4_out_7, video_subsystem_4_out_8,
       video_subsystem_4_out_9, video_subsystem_4_out_10, video_subsystem_4_out_11, video_subsystem_4_out_12,
       video_subsystem_4_out_13;

  Joystick #(.bits(5)) joystick_1 (.y(joystick_1_y));  // open: x
  Joystick #(.bits(5)) joystick_2 (.y(joystick_2_y));  // open: x
  Button R (.out(R_out));
  assign not_1_out = ~joystick_1_y;  // NOT_Gate not_1, 5 bits wide
  Clock clock_1 (.out(clock_1_out));
  Hex_Digit_Display hex_digit_display_1 (.value(A));  // open: dp
  assign not_2_out = ~joystick_2_y;  // NOT_Gate not_2, 5 bits wide
  DotMatrix #(.matrixcols(32), .matrixrows(32)) dotmatrix_1 (
    .col0(video_subsystem_1_out_6), .col1(video_subsystem_1_out_7), .col2(video_subsystem_1_out_8),
    .col3(video_subsystem_1_out_9), .col4(video_subsystem_1_out_10), .col5(video_subsystem_1_out_11),
    .col6(video_subsystem_1_out_12), .col7(video_subsystem_1_out_13), .col8(video_subsystem_2_out_6),
    .col9(video_subsystem_2_out_7), .col10(video_subsystem_2_out_8), .col11(video_subsystem_2_out_9),
    .col12(video_subsystem_2_out_10), .col13(video_subsystem_2_out_11), .col14(video_subsystem_2_out_12),
    .col15(video_subsystem_2_out_13), .col16(video_subsystem_3_out_6), .col17(video_subsystem_3_out_7),
    .col18(video_subsystem_3_out_8), .col19(video_subsystem_3_out_9), .col20(video_subsystem_3_out_10),
    .col21(video_subsystem_3_out_11), .col22(video_subsystem_3_out_12), .col23(video_subsystem_3_out_13),
    .col24(video_subsystem_4_out_6), .col25(video_subsystem_4_out_7), .col26(video_subsystem_4_out_8),
    .col27(video_subsystem_4_out_9), .col28(video_subsystem_4_out_10), .col29(video_subsystem_4_out_11),
    .col30(video_subsystem_4_out_12), .col31(video_subsystem_4_out_13));
  kinematic kinematic_1 (
    .R_bat(not_1_out), .reset(R_out), .L_bat(not_2_out), .clock(clock_1_out), .A_score(A), .B_score(B),
    .cheap_ID(kinematic_1_cheap_id), .X_ball1(kinematic_1_x_ball1), .Y_ball1(kinematic_1_y_ball1),
    .l_bat_2(kinematic_1_l_bat_2), .r_bat_2(kinematic_1_r_bat_2));  // open: X_ball, Y_ball, vxy
  video_subsystem video_subsystem_1 (
    .cheapID(kinematic_1_cheap_id), .ballX(kinematic_1_x_ball1), .ballY(kinematic_1_y_ball1),
    .leftBatY(kinematic_1_l_bat_2), .rightBatY(kinematic_1_r_bat_2), .cheapID_2(video_subsystem_1_cheapid_2),
    .ballX_2(video_subsystem_1_ballx_2), .ballY_2(video_subsystem_1_bally_2),
    .leftBatY_2(video_subsystem_1_leftbaty_2), .rightBatY_2(video_subsystem_1_rightbaty_2),
    .out_6(video_subsystem_1_out_6), .out_7(video_subsystem_1_out_7), .out_8(video_subsystem_1_out_8),
    .out_9(video_subsystem_1_out_9), .out_10(video_subsystem_1_out_10), .out_11(video_subsystem_1_out_11),
    .out_12(video_subsystem_1_out_12), .out_13(video_subsystem_1_out_13));
  video_subsystem video_subsystem_2 (
    .cheapID(video_subsystem_1_cheapid_2), .ballX(video_subsystem_1_ballx_2),
    .ballY(video_subsystem_1_bally_2), .leftBatY(video_subsystem_1_leftbaty_2),
    .rightBatY(video_subsystem_1_rightbaty_2), .cheapID_2(video_subsystem_2_cheapid_2),
    .ballX_2(video_subsystem_2_ballx_2), .ballY_2(video_subsystem_2_bally_2),
    .leftBatY_2(video_subsystem_2_leftbaty_2), .rightBatY_2(video_subsystem_2_rightbaty_2),
    .out_6(video_subsystem_2_out_6), .out_7(video_subsystem_2_out_7), .out_8(video_subsystem_2_out_8),
    .out_9(video_subsystem_2_out_9), .out_10(video_subsystem_2_out_10), .out_11(video_subsystem_2_out_11),
    .out_12(video_subsystem_2_out_12), .out_13(video_subsystem_2_out_13));
  video_subsystem video_subsystem_3 (
    .cheapID(video_subsystem_2_cheapid_2), .ballX(video_subsystem_2_ballx_2),
    .ballY(video_subsystem_2_bally_2), .leftBatY(video_subsystem_2_leftbaty_2),
    .rightBatY(video_subsystem_2_rightbaty_2), .cheapID_2(video_subsystem_3_cheapid_2),
    .ballX_2(video_subsystem_3_ballx_2), .ballY_2(video_subsystem_3_bally_2),
    .leftBatY_2(video_subsystem_3_leftbaty_2), .rightBatY_2(video_subsystem_3_rightbaty_2),
    .out_6(video_subsystem_3_out_6), .out_7(video_subsystem_3_out_7), .out_8(video_subsystem_3_out_8),
    .out_9(video_subsystem_3_out_9), .out_10(video_subsystem_3_out_10), .out_11(video_subsystem_3_out_11),
    .out_12(video_subsystem_3_out_12), .out_13(video_subsystem_3_out_13));
  video_subsystem video_subsystem_4 (
    .cheapID(video_subsystem_3_cheapid_2), .ballX(video_subsystem_3_ballx_2),
    .ballY(video_subsystem_3_bally_2), .leftBatY(video_subsystem_3_leftbaty_2),
    .rightBatY(video_subsystem_3_rightbaty_2), .out_6(video_subsystem_4_out_6),
    .out_7(video_subsystem_4_out_7), .out_8(video_subsystem_4_out_8), .out_9(video_subsystem_4_out_9),
    .out_10(video_subsystem_4_out_10), .out_11(video_subsystem_4_out_11), .out_12(video_subsystem_4_out_12),
    .out_13(video_subsystem_4_out_13));  // open: cheapID_2, ballX_2, ballY_2, leftBatY_2, rightBatY_2
  Hex_Digit_Display hex_digit_display_2 (.value(B));  // open: dp
endmodule

module video_subsystem (
  input  [4:0] cheapID,
  input  [4:0] ballX,
  input  [4:0] ballY,
  input  [4:0] leftBatY,
  input  [4:0] rightBatY,
  output [31:0] out_6,
  output [31:0] out_7,
  output [31:0] out_8,
  output [31:0] out_9,
  output [31:0] out_10,
  output [31:0] out_11,
  output [31:0] out_12,
  output [31:0] out_13,
  output [4:0] cheapID_2,
  output [4:0] ballX_2,
  output [4:0] ballY_2,
  output [4:0] leftBatY_2,
  output [4:0] rightBatY_2
);

  wire [4:0] video_chip_1_ballx_2, video_chip_1_bally_2, video_chip_1_chipid_2, video_chip_1_leftbaty_2,
       video_chip_1_rightbaty_2, video_chip_2_ballx_2, video_chip_2_bally_2, video_chip_2_chipid_2,
       video_chip_2_leftbaty_2, video_chip_2_rightbaty_2, video_chip_3_ballx_2, video_chip_3_bally_2,
       video_chip_3_chipid_2, video_chip_3_leftbaty_2, video_chip_3_rightbaty_2, video_chip_4_ballx_2,
       video_chip_4_bally_2, video_chip_4_chipid_2, video_chip_4_leftbaty_2, video_chip_4_rightbaty_2,
       video_chip_5_ballx_2, video_chip_5_bally_2, video_chip_5_chipid_2, video_chip_5_leftbaty_2,
       video_chip_5_rightbaty_2, video_chip_6_ballx_2, video_chip_6_bally_2, video_chip_6_chipid_2,
       video_chip_6_leftbaty_2, video_chip_6_rightbaty_2, video_chip_7_ballx_2, video_chip_7_bally_2,
       video_chip_7_chipid_2, video_chip_7_leftbaty_2, video_chip_7_rightbaty_2;

  video_chip video_chip_1 (
    .chipID(cheapID), .ballX(ballX), .ballY(ballY), .leftbatY(leftBatY), .rightbatY(rightBatY),
    .chipID_2(video_chip_1_chipid_2), .ballX_2(video_chip_1_ballx_2), .ballY_2(video_chip_1_bally_2),
    .leftbatY_2(video_chip_1_leftbaty_2), .rightbatY_2(video_chip_1_rightbaty_2), .out(out_6));
  video_chip video_chip_2 (
    .chipID(video_chip_1_chipid_2), .ballX(video_chip_1_ballx_2), .ballY(video_chip_1_bally_2),
    .leftbatY(video_chip_1_leftbaty_2), .rightbatY(video_chip_1_rightbaty_2),
    .chipID_2(video_chip_2_chipid_2), .ballX_2(video_chip_2_ballx_2), .ballY_2(video_chip_2_bally_2),
    .leftbatY_2(video_chip_2_leftbaty_2), .rightbatY_2(video_chip_2_rightbaty_2), .out(out_7));
  video_chip video_chip_3 (
    .chipID(video_chip_2_chipid_2), .ballX(video_chip_2_ballx_2), .ballY(video_chip_2_bally_2),
    .leftbatY(video_chip_2_leftbaty_2), .rightbatY(video_chip_2_rightbaty_2),
    .chipID_2(video_chip_3_chipid_2), .ballX_2(video_chip_3_ballx_2), .ballY_2(video_chip_3_bally_2),
    .leftbatY_2(video_chip_3_leftbaty_2), .rightbatY_2(video_chip_3_rightbaty_2), .out(out_8));
  video_chip video_chip_4 (
    .chipID(video_chip_3_chipid_2), .ballX(video_chip_3_ballx_2), .ballY(video_chip_3_bally_2),
    .leftbatY(video_chip_3_leftbaty_2), .rightbatY(video_chip_3_rightbaty_2),
    .chipID_2(video_chip_4_chipid_2), .ballX_2(video_chip_4_ballx_2), .ballY_2(video_chip_4_bally_2),
    .leftbatY_2(video_chip_4_leftbaty_2), .rightbatY_2(video_chip_4_rightbaty_2), .out(out_9));
  video_chip video_chip_5 (
    .chipID(video_chip_4_chipid_2), .ballX(video_chip_4_ballx_2), .ballY(video_chip_4_bally_2),
    .leftbatY(video_chip_4_leftbaty_2), .rightbatY(video_chip_4_rightbaty_2),
    .chipID_2(video_chip_5_chipid_2), .ballX_2(video_chip_5_ballx_2), .ballY_2(video_chip_5_bally_2),
    .leftbatY_2(video_chip_5_leftbaty_2), .rightbatY_2(video_chip_5_rightbaty_2), .out(out_10));
  video_chip video_chip_6 (
    .chipID(video_chip_5_chipid_2), .ballX(video_chip_5_ballx_2), .ballY(video_chip_5_bally_2),
    .leftbatY(video_chip_5_leftbaty_2), .rightbatY(video_chip_5_rightbaty_2),
    .chipID_2(video_chip_6_chipid_2), .ballX_2(video_chip_6_ballx_2), .ballY_2(video_chip_6_bally_2),
    .leftbatY_2(video_chip_6_leftbaty_2), .rightbatY_2(video_chip_6_rightbaty_2), .out(out_11));
  video_chip video_chip_7 (
    .chipID(video_chip_6_chipid_2), .ballX(video_chip_6_ballx_2), .ballY(video_chip_6_bally_2),
    .leftbatY(video_chip_6_leftbaty_2), .rightbatY(video_chip_6_rightbaty_2),
    .chipID_2(video_chip_7_chipid_2), .ballX_2(video_chip_7_ballx_2), .ballY_2(video_chip_7_bally_2),
    .leftbatY_2(video_chip_7_leftbaty_2), .rightbatY_2(video_chip_7_rightbaty_2), .out(out_12));
  video_chip video_chip_8 (
    .chipID(video_chip_7_chipid_2), .ballX(video_chip_7_ballx_2), .ballY(video_chip_7_bally_2),
    .leftbatY(video_chip_7_leftbaty_2), .rightbatY(video_chip_7_rightbaty_2), .chipID_2(cheapID_2),
    .ballX_2(ballX_2), .ballY_2(ballY_2), .leftbatY_2(leftBatY_2), .rightbatY_2(rightBatY_2), .out(out_13));
endmodule

module video_chip (
  input  [4:0] chipID,
  input  [4:0] ballX,
  input  [4:0] ballY,
  input  [4:0] leftbatY,
  input  [4:0] rightbatY,
  output [4:0] chipID_2,
  output [4:0] ballX_2,
  output [4:0] ballY_2,
  output [4:0] leftbatY_2,
  output [4:0] rightbatY_2,
  output [31:0] out
);

  wire comparator_1_eq, comparator_2_eq, comparator_3_eq;
  wire [31:0] multiplexer_1_out, multiplexer_2_out, multiplexer_3_out, shifter_1_out, shifter_2_out,
       shifter_3_out;

  Comparator #(.width(5)) comparator_1 (.a(chipID), .b(ballX), .eq(comparator_1_eq));  // open: gt, lt
  Comparator #(.width(5)) comparator_2 (.a(chipID), .b(5'b00011), .eq(comparator_2_eq));  // open: gt, lt
  Comparator #(.width(5)) comparator_3 (.a(5'b11100), .b(chipID), .eq(comparator_3_eq));  // open: gt, lt
  Adder #(.width(5)) adder_1 (.a(5'b00001), .b(chipID), .out(chipID_2));  // open: cin, cout
  Shifter #(.width(32)) shifter_1 (.in(32'h7), .\dist (leftbatY), .out(shifter_1_out));
  Shifter #(.width(32)) shifter_2 (.in(32'h7), .\dist (rightbatY), .out(shifter_2_out));
  Multiplexer #(.width(32), .enable("false")) multiplexer_1 (
    .in0({32{1'b0}}), .in1(shifter_1_out), .out(multiplexer_1_out), .sel(comparator_2_eq));
  Shifter #(.width(32)) shifter_3 (.in(32'h1), .\dist (ballY), .out(shifter_3_out));
  Multiplexer #(.width(32), .enable("false")) multiplexer_2 (
    .in0(multiplexer_1_out), .in1(shifter_2_out), .out(multiplexer_2_out), .sel(comparator_3_eq));
  Multiplexer #(.width(32), .enable("false")) multiplexer_3 (
    .in0({32{1'b0}}), .in1(shifter_3_out), .out(multiplexer_3_out), .sel(comparator_1_eq));
  // Probe on multiplexer_3_out
  // Probe on multiplexer_2_out
  assign out = multiplexer_3_out | multiplexer_2_out;  // OR_Gate or_1, 32 bits wide

  assign ballX_2 = ballX;
  assign ballY_2 = ballY;
  assign leftbatY_2 = leftbatY;
  assign rightbatY_2 = rightbatY;
endmodule

module kinematic (
  input  reset,
  input  [4:0] L_bat,
  input  [4:0] R_bat,
  input  clock,
  output [4:0] cheap_ID,
  output [7:0] X_ball,
  output [4:0] X_ball1,
  output [4:0] Y_ball1,
  output [7:0] Y_ball,
  output [4:0] l_bat_2,
  output [4:0] r_bat_2,
  output [7:0] vxy,
  output [3:0] A_score,
  output [3:0] B_score
);

  wire adder_1_cout, adder_2_cout, adder_7_cout, adder_8_cout, and_1_out, ball_contact_with_bat_1_bal_refl,
       ball_contact_with_bat_2_bal_refl, comparator_1_eq, comparator_2_eq, comparator_3_eq, comparator_4_eq,
       hit_Left_Side, hit_Right_Side, justContactWithBat, leftBatContact, not_3_out, not_6_out, not_7_out,
       not_8_out, or_1_out, or_2_out, relfX, relfY, righttBatContact;
  wire [2:0] multiplexer_5_out, multiplexer_6_out, not_4_out, not_5_out;
  wire [3:0] adder_3_out, adder_4_out, register_1_q, register_2_q;
  wire [7:0] adder_1_out, adder_2_out, adder_5_out, adder_6_out, multiplexer_3_out, multiplexer_4_out;

  Adder adder_1 (.a({{6{vxy[2]}}, vxy[1:0]}), .b(Y_ball), .out(adder_1_out), .cout(adder_1_cout));  // open: cin
  not not_1 (relfY, comparator_1_eq);
  Adder adder_2 (.a({{6{vxy[5]}}, vxy[4:3]}), .b(X_ball), .out(adder_2_out), .cout(adder_2_cout));  // open: cin
  not not_2 (relfX, comparator_2_eq);
  Register #(.width(4)) register_1 (.D(A_score), .en(hit_Right_Side), .Q(register_1_q), .clk(clock), .clr(reset));
  Register #(.width(4)) register_2 (.D(B_score), .en(hit_Left_Side), .Q(register_2_q), .clk(clock), .clr(reset));
  Comparator #(.width(1)) comparator_1 (.a(adder_1_cout), .b(vxy[2]), .eq(comparator_1_eq));  // open: gt, lt
  Comparator #(.width(1)) comparator_2 (.a(adder_2_cout), .b(vxy[5]), .eq(comparator_2_eq));  // open: gt, lt
  not not_3 (not_3_out, justContactWithBat);
  Multiplexer #(.width(4), .disabled(0), .enable("false")) multiplexer_1 (
    .in0(register_1_q), .in1(adder_3_out), .out(A_score), .sel(hit_Right_Side));
  Adder #(.width(4)) adder_3 (.a(register_1_q), .b(4'b0001), .out(adder_3_out));  // open: cin, cout
  Multiplexer #(.width(4), .disabled(0), .enable("false")) multiplexer_2 (
    .in0(register_2_q), .in1(adder_4_out), .out(B_score), .sel(hit_Left_Side));
  Adder #(.width(4)) adder_4 (.a(register_2_q), .b(4'b0001), .out(adder_4_out));  // open: cin, cout
  Multiplexer #(.width(8), .disabled(0), .enable("false")) multiplexer_3 (
    .in0(adder_1_out), .in1(8'h80), .out(multiplexer_3_out), .sel(reset));
  Multiplexer #(.width(8), .disabled(0), .enable("false")) multiplexer_4 (
    .in0(adder_2_out), .in1(8'h80), .out(multiplexer_4_out), .sel(reset));
  and and_1 (and_1_out, comparator_2_eq, not_3_out);
  Register register_3 (.D(multiplexer_3_out), .en(comparator_1_eq), .Q(Y_ball), .clk(clock));  // open: clr
  Register register_4 (.D(multiplexer_4_out), .en(and_1_out), .Q(X_ball), .clk(clock));  // open: clr
  assign not_4_out = ~vxy[2:0];  // NOT_Gate not_4, 3 bits wide
  assign not_5_out = ~vxy[5:3];  // NOT_Gate not_5, 3 bits wide
  Multiplexer #(.width(3), .disabled(0), .enable("false")) multiplexer_5 (
    .in0(not_4_out), .in1(3'b001), .out(multiplexer_5_out), .sel(reset));
  or or_1 (or_1_out, relfY, reset);
  Multiplexer #(.width(3), .disabled(0), .enable("false")) multiplexer_6 (
    .in0(not_5_out), .in1(3'b101), .out(multiplexer_6_out), .sel(reset));
  or or_2 (or_2_out, relfX, justContactWithBat, reset);
  Register #(.width(3)) register_5 (.D(multiplexer_5_out), .en(or_1_out), .Q(vxy[2:0]), .clk(clock));  // open: clr
  Register #(.width(3)) register_6 (.D(multiplexer_6_out), .en(or_2_out), .Q(vxy[5:3]), .clk(clock));  // open: clr
  and and_2 (hit_Left_Side, relfX, vxy[5]);
  Adder adder_5 (.a(X_ball), .b(8'he4), .out(adder_5_out));  // open: cin, cout
  Adder adder_6 (.a(X_ball), .b(8'h1c), .out(adder_6_out));  // open: cin, cout
  or or_3 (justContactWithBat, righttBatContact, leftBatContact);
  Adder adder_7 (.a(adder_5_out), .b({{6{vxy[5]}}, vxy[4:3]}), .cout(adder_7_cout));  // open: out, cin
  not not_6 (not_6_out, comparator_3_eq);
  Comparator #(.width(1)) comparator_3 (.a(adder_7_cout), .b(vxy[5]), .eq(comparator_3_eq));  // open: gt, lt
  ball_contact_with_bat ball_contact_with_bat_1 (
    .bat(L_bat), .Ycoor(Y_ball), .bal_refl(ball_contact_with_bat_1_bal_refl));
  Adder adder_8 (.a(adder_6_out), .b({{6{vxy[5]}}, vxy[4:3]}), .cout(adder_8_cout));  // open: out, cin
  not not_7 (not_7_out, comparator_4_eq);
  Comparator #(.width(1)) comparator_4 (.a(adder_8_cout), .b(vxy[5]), .eq(comparator_4_eq));  // open: gt, lt
  ball_contact_with_bat ball_contact_with_bat_2 (
    .bat(R_bat), .Ycoor(Y_ball), .bal_refl(ball_contact_with_bat_2_bal_refl));
  and and_3 (leftBatContact, not_6_out, ball_contact_with_bat_1_bal_refl);
  and and_4 (righttBatContact, not_7_out, ball_contact_with_bat_2_bal_refl);
  and and_5 (hit_Right_Side, relfX, not_8_out);
  not not_8 (not_8_out, vxy[5]);

  assign cheap_ID = {5{1'b0}};
  assign l_bat_2 = L_bat;
  assign r_bat_2 = R_bat;
  assign vxy[7:6] = 2'b00;
  assign X_ball1 = X_ball[7:3];
  assign Y_ball1 = Y_ball[7:3];

  // Other names for the same wires on the sheet: Lbat[4:0] = L_bat; Rbat[4:0] = R_bat; scoreA[3:0] = A_score;
  //   scoreB[3:0] = B_score; _3bitVX[2:0] = vxy[5:3]; vx[7:0] = {{6{vxy[5]}}, vxy[4:3]}; complVX = vxy[5];
  //   _3bitVY[2:0] = vxy[2:0]; vy[7:0] = {{6{vxy[2]}}, vxy[1:0]}; complVY = vxy[2]; Xcoor[7:0] = X_ball;
  //   Ycoor[7:0] = Y_ball
endmodule

module ball_contact_with_bat (
  input  [4:0] bat,
  input  [7:0] Ycoor,
  output bal_refl
);

  wire comparator_1_eq, comparator_2_eq, comparator_3_eq;
  wire [4:0] adder_1_out, adder_2_out;

  Adder #(.width(5)) adder_1 (.a(bat), .b(5'b00001), .out(adder_1_out));  // open: cin, cout
  Adder #(.width(5)) adder_2 (.a(bat), .b(5'b00010), .out(adder_2_out));  // open: cin, cout
  Comparator #(.width(5)) comparator_1 (.a(bat), .b(Ycoor[7:3]), .eq(comparator_1_eq));  // open: gt, lt
  Comparator #(.width(5)) comparator_2 (.a(adder_1_out), .b(Ycoor[7:3]), .eq(comparator_2_eq));  // open: gt, lt
  Comparator #(.width(5)) comparator_3 (.a(adder_2_out), .b(Ycoor[7:3]), .eq(comparator_3_eq));  // open: gt, lt
  or or_1 (bal_refl, comparator_1_eq, comparator_2_eq, comparator_3_eq);
endmodule
